// Logisim project adder.circ as structural Verilog: 4 circuits, main circuit main
module half_adder (
  input  A,
  input  B,
  output C,
  output S
);

  and and_1 (C, A, B);
  xor xor_1 (S, A, B);
endmodule

module full_adder (
  input  C_in,
  input  A,
  input  B,
  output Sum,
  output C_out
);

  wire and_1_out, and_2_out, xor_1_out;

  and and_1 (and_1_out, B, A);
  xor xor_1 (xor_1_out, A, B);
  or or_1 (C_out, and_1_out, and_2_out);
  and and_2 (and_2_out, xor_1_out, C_in);
  xor xor_2 (Sum, C_in, xor_1_out);
endmodule

module _4_bit_adder (
  input  in_1,
  input  in_2,
  input  in_3,
  input  in_4,
  input  A3,
  input  A2,
  input  A1,
  input  A0,
  input  sub,
  input  C_in,
  output C_out,
  output S4,
  output S3,
  output S2,
  output S1,
  output out_16
);

  wire full_adder_2_c_out, full_adder_3_c_out, full_adder_4_c_out, or_1_out, xor_1_out, xor_3_out, xor_4_out,
       xor_5_out;

  xor xor_1 (xor_1_out, in_1, sub);
  full_adder full_adder_1 (.A(A3), .B(xor_1_out), .Sum(S4), .C_in(full_adder_2_c_out), .C_out(C_out));
  xor xor_2 (out_16, C_out, full_adder_2_c_out);
  xor xor_3 (xor_3_out, in_2, sub);
  full_adder full_adder_2 (.A(A2), .B(xor_3_out), .Sum(S3), .C_in(full_adder_3_c_out), .C_out(full_adder_2_c_out));
  xor xor_4 (xor_4_out, in_3, sub);
  full_adder full_adder_3 (.A(A1), .B(xor_4_out), .Sum(S2), .C_in(full_adder_4_c_out), .C_out(full_adder_3_c_out));
  full_adder full_adder_4 (.A(A0), .B(xor_5_out), .Sum(S1), .C_in(or_1_out), .C_out(full_adder_4_c_out));
  xor xor_5 (xor_5_out, sub, in_4);
  or or_1 (or_1_out, sub, C_in);
endmodule

module main (
  input  [15:0] A,
  input  [15:0] B,
  input  sub,
  output ovf,
  output [15:0] result
);

  wire n4_bit_adder_2_c_out, n4_bit_adder_3_c_out, n4_bit_adder_4_c_out;

  _4_bit_adder u_4_bit_adder_1 (
    .A0(A[12]), .A3(A[15]), .in_1(B[15]), .A2(A[14]), .in_2(B[14]), .A1(A[13]), .in_3(B[13]), .in_4(B[12]),
    .S4(result[15]), .S3(result[14]), .S2(result[13]), .S1(result[12]), .sub(sub),
    .C_in(n4_bit_adder_2_c_out), .out_16(ovf));  // open: C_out
  _4_bit_adder u_4_bit_adder_2 (
    .A0(A[8]), .A3(A[11]), .in_1(B[11]), .A2(A[10]), .in_2(B[10]), .A1(A[9]), .in_3(B[9]), .in_4(B[8]),
    .C_out(n4_bit_adder_2_c_out), .S4(result[11]), .S3(result[10]), .S2(result[9]), .S1(result[8]),
    .sub(sub), .C_in(n4_bit_adder_3_c_out));  // open: out_16
  _4_bit_adder u_4_bit_adder_3 (
    .A0(A[4]), .A3(A[7]), .in_1(B[7]), .A2(A[6]), .in_2(B[6]), .A1(A[5]), .in_3(B[5]), .in_4(B[4]),
    .C_out(n4_bit_adder_3_c_out), .S4(result[7]), .S3(result[6]), .S2(result[5]), .S1(result[4]), .sub(sub),
    .C_in(n4_bit_adder_4_c_out));  // open: out_16
  _4_bit_adder u_4_bit_adder_4 (
    .A0(A[0]), .A3(A[3]), .in_1(B[3]), .A2(A[2]), .in_2(B[2]), .A1(A[1]), .in_3(B[1]), .in_4(B[0]),
    .C_out(n4_bit_adder_4_c_out), .S4(result[3]), .S3(result[2]), .S2(result[1]), .S1(result[0]), .sub(sub),
    .C_in(1'b0));  // open: out_16
endmodule
