// Logisim project circuit1a.circ as structural Verilog: 1 circuit, main circuit main
module main (
  input  A,
  input  B,
  input  C,
  output out
);

  wire and_1_out, and_2_out, and_3_out, or_1_out, or_2_out;

  and and_1 (and_1_out, A, B);
  and and_2 (and_2_out, B, C);
  or or_1 (or_1_out, A, B);
  and and_3 (and_3_out, or_1_out, C);
  or or_2 (or_2_out, and_1_out, and_2_out);
  or or_3 (out, and_3_out, or_2_out);
endmodule
