// Logisim project plastic.circ as structural Verilog: 3 circuits, main circuit main
module main (
  input  temp_ok,
  input  go,
  output heater,
  output extruder
);

  wire clk, D0, D1, Not_Q0, Not_Q1, Q0, Q1;

  Clock clock_1 (.out(clk));
  D1 d1_1 (.temp_ok(temp_ok), .Q0(Q0), .Q1(Q1), .D1(D1));
  D0 d0_1 (.temp_ok(temp_ok), .go(go), .Q0(Q0), .Q1(Q1), .D1(D0));
  D_Flip_Flop u_Q1 (.clk(clk), .D(D1), .Q(Q1), .Qn(Not_Q1));  // open: preset, en, reset
  D_Flip_Flop u_Q0 (.clk(clk), .D(D0), .Q(Q0), .Qn(Not_Q0));  // open: preset, en, reset
  and and_1 (heater, Not_Q1, Q0);
  and and_2 (extruder, Q1, Q0);
endmodule

module D1 (
  input  temp_ok,
  input  Q0,
  input  Q1,
  output D1
);

  wire _1_out, _2_out, not_1_out;

  not not_1 (not_1_out, Q0);
  and _1 (_1_out, temp_ok, Q0);
  and _2 (_2_out, not_1_out, temp_ok, Q1);
  or or_1 (D1, _1_out, _2_out);
endmodule

module D0 (
  input  temp_ok,
  input  go,
  input  Q0,
  input  Q1,
  output D1
);

  wire _1_out, _2_out, _3_out, _4_out, not_1_out, not_2_out, not_3_out, not_4_out, not_5_out, not_6_out;

  not not_1 (not_1_out, Q0);
  and _1 (_1_out, Q0, not_2_out);
  not not_2 (not_2_out, temp_ok);
  not not_3 (not_3_out, Q1);
  not not_4 (not_4_out, Q0);
  and _2 (_2_out, not_3_out, not_4_out, go);
  not not_5 (not_5_out, Q0);
  and _3 (_3_out, Q1, not_5_out, not_6_out);
  not not_6 (not_6_out, temp_ok);
  and _4 (_4_out, Q1, not_1_out, go, temp_ok);
  or or_1 (D1, _1_out, _2_out, _3_out, _4_out);
endmodule
