// Logisim project cpu.circ as structural Verilog: 10 circuits, main circuit main
// Register File
module main (
  input  reset
);

  wire alu_1_overflow, alu_1_remain, alu_1_z, ALUinB, Bne, BR, clk, DMwe, In, Jal, JP, Jr, keyboard_1_avail,
       multiplexer_6_out, not_2_out, Out, Rdst, Rwd, Rwe, xor_1_out;
  wire [2:0] ALUOpCode, multiplexer_3_out, multiplexer_4_out, rd, rs, rt, shamt;
  wire [3:0] decoder_1_opcode;
  wire [5:0] immed;
  wire [6:0] keyboard_1_data;
  wire [7:7] not_1_out;
  wire [11:0] address;
  wire [15:0] alu_1_outputdata, bit_extender_2_out, bit_extender_3_out, inResult, multiplexer_1_out,
       multiplexer_2_out, multiplexer_5_out, multiplexer_7_out, multiplexer_8_out, multiplexer_9_out,
       multiplexer_10_out, n16_bit_adder_1_result, n16_bit_adder_2_result, PC_output, ram_1_data, rom_1_data,
       rsOutput, Sw;

  Keyboard keyboard_1 (.clk(clk), .re(In), .clr(reset), .avail(keyboard_1_avail), .data(keyboard_1_data));
  _16_bit_register PC (
    .\input (multiplexer_10_out), .\output (PC_output), .Write_Enable(1'b1), .reset(reset), .clk(clk));
  Clock clock_1 (.out(clk));
  not not_1 (not_1_out[7], keyboard_1_avail);
  assign inResult = {{8{not_1_out[7]}}, {not_1_out[7], keyboard_1_data}};  // Bit_Extender bit_extender_1
  _16_bit_adder u_16_bit_adder_1 (
    .sub(1'b0), .B(16'h1), .A(PC_output), .Result(n16_bit_adder_1_result));  // open: C_out, ovf
  TTY #(.rows(13), .cols(80), .trigger("falling")) tty_1 (.data(rsOutput[6:0]), .clk(clk), .we(Out), .clr(reset));
  ROM #(.addrWidth(16), .dataWidth(16)) rom_1 (.addr(PC_output), .data(rom_1_data));  // open: sel
  Decoder decoder_1 (
    .Input(rom_1_data), .Opcode(decoder_1_opcode), .Address(address), .Rs(rs), .Rt(rt), .Rd(rd),
    .Shamt(shamt), .Immediate(immed));
  Control control_1 (
    .jal(Jal), .opcode(decoder_1_opcode), .Rwe(Rwe), .ALUinB(ALUinB), .Rdst(Rdst), .BR(BR), .JP(JP),
    .DMwe(DMwe), .ALUOpCode(ALUOpCode), .Rwd(Rwd), .Bne_2(Bne), .Jr_2(Jr), .In(In), .Out(Out));  // open: add, addi, sub, not, xor, sll, srl, lw, sw, bne, blt, j, jr, input, output
  Multiplexer #(.width(16), .enable("false")) multiplexer_1 (
    .in0(multiplexer_2_out), .in1(n16_bit_adder_1_result), .out(multiplexer_1_out), .sel(Jal));
  Multiplexer #(.width(16), .enable("false")) multiplexer_2 (
    .in0(multiplexer_9_out), .in1(inResult), .out(multiplexer_2_out), .sel(In));
  RegisterFile registerfile_1 (
    .reset(reset), .rs(rs), .rt(rt), .rd(multiplexer_3_out), .clk(clk), .rdval(multiplexer_1_out),
    .rsval(rsOutput), .rtval(Sw), .we(Rwe));
  Multiplexer #(.width(3), .enable("false")) multiplexer_3 (
    .in0(multiplexer_4_out), .in1(3'b111), .out(multiplexer_3_out), .sel(Jal));
  Multiplexer #(.width(3), .enable("false")) multiplexer_4 (.in0(rd), .in1(rt), .out(multiplexer_4_out), .sel(Rdst));
  assign bit_extender_2_out = {{10{immed[5]}}, immed};  // Bit_Extender bit_extender_2
  ALU alu_1 (
    .InputData1(rsOutput), .InputData2(multiplexer_5_out), .ALUOpType(ALUOpCode),
    .OutputData(alu_1_outputdata), .Shift_Amount(shamt), .Z(alu_1_z), .Overflow(alu_1_overflow),
    .Remain(alu_1_remain));
  Multiplexer #(.width(16), .enable("false")) multiplexer_5 (
    .in0(Sw), .in1(bit_extender_2_out), .out(multiplexer_5_out), .sel(ALUinB));
  _16_bit_adder u_16_bit_adder_2 (
    .sub(1'b0), .B(bit_extender_2_out), .A(n16_bit_adder_1_result), .Result(n16_bit_adder_2_result));  // open: C_out, ovf
  Multiplexer #(.disabled(0)) multiplexer_6 (
    .in0(xor_1_out), .in1(alu_1_z), .out(multiplexer_6_out), .sel(Bne), .en(BR));
  xor xor_1 (xor_1_out, alu_1_overflow, alu_1_remain);
  Multiplexer #(.width(16), .enable("false")) multiplexer_7 (
    .in0(n16_bit_adder_1_result), .in1(n16_bit_adder_2_result), .out(multiplexer_7_out),
    .sel(multiplexer_6_out));
  Multiplexer #(.width(16), .enable("false")) multiplexer_8 (
    .in0(multiplexer_7_out), .in1(bit_extender_3_out), .out(multiplexer_8_out), .sel(JP));
  assign bit_extender_3_out = {{4{address[11]}}, address};  // Bit_Extender bit_extender_3
  RAM #(.addrWidth(16), .dataWidth(16), .bus("separate")) ram_1 (
    .addr(alu_1_outputdata), .din(Sw), .data(ram_1_data), .str(DMwe), .clk(not_2_out));  // open: sel, ld, clr
  not not_2 (not_2_out, clk);
  Multiplexer #(.width(16), .enable("false")) multiplexer_9 (
    .in0(alu_1_outputdata), .in1(ram_1_data), .out(multiplexer_9_out), .sel(Rwd));
  Multiplexer #(.width(16), .enable("false")) multiplexer_10 (
    .in0(multiplexer_8_out), .in1(rsOutput), .out(multiplexer_10_out), .sel(Jr));

  // Other names for the same wires on the sheet: rsval[15:0] = rsOutput

  // Notes on the sheet:
  //   Input
  //   contents of rom_1 (hex, n*v repeats v):
  //   104f 1090 10ca a457 a284 1194 91ff 1fc1 91ff d010 92d0 920a 1195 91ff 1fc1 91ff 127b ce00 1196 91ff
  //   1fc1 91ff b018 1197 91ff 1fc1 91ff 1198 91ff 1fc1 91ff
  //   Output
  //   Data Memory
endmodule

module _16_bit_register (
  input  [15:0] \input ,
  input  clk,
  input  Write_Enable,
  input  reset,
  output [15:0] \output 
);

  D_Flip_Flop d_ff_1 (
    .clk(clk), .D(\input [0]), .Q(\output [0]), .en(Write_Enable), .reset(reset));  // open: Qn, preset
  D_Flip_Flop d_ff_2 (
    .clk(clk), .D(\input [1]), .Q(\output [1]), .en(Write_Enable), .reset(reset));  // open: Qn, preset
  D_Flip_Flop d_ff_3 (
    .clk(clk), .D(\input [2]), .Q(\output [2]), .en(Write_Enable), .reset(reset));  // open: Qn, preset
  D_Flip_Flop d_ff_4 (
    .clk(clk), .D(\input [3]), .Q(\output [3]), .en(Write_Enable), .reset(reset));  // open: Qn, preset
  D_Flip_Flop d_ff_5 (
    .clk(clk), .D(\input [4]), .Q(\output [4]), .en(Write_Enable), .reset(reset));  // open: Qn, preset
  D_Flip_Flop d_ff_6 (
    .clk(clk), .D(\input [5]), .Q(\output [5]), .en(Write_Enable), .reset(reset));  // open: Qn, preset
  D_Flip_Flop d_ff_7 (
    .clk(clk), .D(\input [6]), .Q(\output [6]), .en(Write_Enable), .reset(reset));  // open: Qn, preset
  D_Flip_Flop d_ff_8 (
    .clk(clk), .D(\input [7]), .Q(\output [7]), .en(Write_Enable), .reset(reset));  // open: Qn, preset
  D_Flip_Flop d_ff_9 (
    .clk(clk), .D(\input [8]), .Q(\output [8]), .en(Write_Enable), .reset(reset));  // open: Qn, preset
  D_Flip_Flop d_ff_10 (
    .clk(clk), .D(\input [9]), .Q(\output [9]), .en(Write_Enable), .reset(reset));  // open: Qn, preset
  D_Flip_Flop d_ff_11 (
    .clk(clk), .D(\input [10]), .Q(\output [10]), .en(Write_Enable), .reset(reset));  // open: Qn, preset
  D_Flip_Flop d_ff_12 (
    .clk(clk), .D(\input [11]), .Q(\output [11]), .en(Write_Enable), .reset(reset));  // open: Qn, preset
  D_Flip_Flop d_ff_13 (
    .clk(clk), .D(\input [12]), .Q(\output [12]), .en(Write_Enable), .reset(reset));  // open: Qn, preset
  D_Flip_Flop d_ff_14 (
    .clk(clk), .D(\input [13]), .Q(\output [13]), .en(Write_Enable), .reset(reset));  // open: Qn, preset
  D_Flip_Flop d_ff_15 (
    .clk(clk), .D(\input [14]), .Q(\output [14]), .en(Write_Enable), .reset(reset));  // open: Qn, preset
  D_Flip_Flop d_ff_16 (
    .clk(clk), .D(\input [15]), .Q(\output [15]), .en(Write_Enable), .reset(reset));  // open: Qn, preset

  // Other names for the same wires on the sheet: R = reset; WE = Write_Enable
endmodule

// Register File
module RegisterFile (
  input  reset,
  input  [2:0] rs,
  input  [2:0] rt,
  input  [2:0] rd,
  input  we,
  input  clk,
  input  [15:0] rdval,
  output [15:0] rsval,
  output [15:0] rtval
);

  wire and_1_out, and_2_out, and_3_out, and_4_out, and_5_out, and_6_out, and_7_out, decoder_1_out1,
       decoder_1_out2, decoder_1_out3, decoder_1_out4, decoder_1_out5, decoder_1_out6, decoder_1_out7,
       decoder_2_out0, decoder_2_out1, decoder_2_out2, decoder_2_out3, decoder_2_out4, decoder_2_out5,
       decoder_2_out6, decoder_2_out7, decoder_3_out0, decoder_3_out1, decoder_3_out2, decoder_3_out3,
       decoder_3_out4, decoder_3_out5, decoder_3_out6, decoder_3_out7;
  wire [15:0] r0, r1, r2, r3, r4, r5, r6, r7;

  Decoder_part #(.select(3), .enable("false")) decoder_1 (
    .out1(decoder_1_out1), .out2(decoder_1_out2), .out3(decoder_1_out3), .out4(decoder_1_out4),
    .out5(decoder_1_out5), .out6(decoder_1_out6), .out7(decoder_1_out7), .sel(rd));  // open: out0
  // Probe on r0
  // Probe on r1
  and and_1 (and_1_out, decoder_1_out1, we);
  // Probe on r2
  and and_2 (and_2_out, decoder_1_out2, we);
  and and_3 (and_3_out, decoder_1_out3, we);
  and and_4 (and_4_out, decoder_1_out4, we);
  and and_5 (and_5_out, decoder_1_out5, we);
  and and_6 (and_6_out, decoder_1_out6, we);
  and and_7 (and_7_out, decoder_1_out7, we);
  // Probe on r3
  _16_bit_register u_16_bit_register_1 (.\input (rdval), .\output (r0), .Write_Enable(1'b0), .reset(reset), .clk(clk));
  _16_bit_register u_16_bit_register_2 (
    .\input (rdval), .\output (r1), .Write_Enable(and_1_out), .reset(reset), .clk(clk));
  _16_bit_register u_16_bit_register_3 (
    .\input (rdval), .\output (r2), .Write_Enable(and_2_out), .reset(reset), .clk(clk));
  _16_bit_register u_16_bit_register_4 (
    .\input (rdval), .\output (r3), .Write_Enable(and_3_out), .reset(reset), .clk(clk));
  _16_bit_register u_16_bit_register_5 (
    .\input (rdval), .\output (r4), .Write_Enable(and_4_out), .reset(reset), .clk(clk));
  _16_bit_register u_16_bit_register_6 (
    .\input (rdval), .\output (r5), .Write_Enable(and_5_out), .reset(reset), .clk(clk));
  _16_bit_register u_16_bit_register_7 (
    .\input (rdval), .\output (r6), .Write_Enable(and_6_out), .reset(reset), .clk(clk));
  _16_bit_register u_16_bit_register_8 (
    .\input (rdval), .\output (r7), .Write_Enable(and_7_out), .reset(reset), .clk(clk));
  // Probe on r4
  // Probe on r5
  // Probe on r6
  assign rsval = decoder_2_out1 ? r1 : 16'bz;  // Controlled_Buffer controlled_buffer_1
  assign rsval = decoder_2_out0 ? r0 : 16'bz;  // Controlled_Buffer controlled_buffer_2
  Decoder_part #(.select(3), .enable("false")) decoder_2 (
    .out0(decoder_2_out0), .out1(decoder_2_out1), .out2(decoder_2_out2), .out3(decoder_2_out3),
    .out4(decoder_2_out4), .out5(decoder_2_out5), .out6(decoder_2_out6), .out7(decoder_2_out7), .sel(rs));
  assign rtval = decoder_3_out1 ? r1 : 16'bz;  // Controlled_Buffer controlled_buffer_3
  assign rtval = decoder_3_out0 ? r0 : 16'bz;  // Controlled_Buffer controlled_buffer_4
  Decoder_part #(.select(3), .enable("false")) decoder_3 (
    .out0(decoder_3_out0), .out1(decoder_3_out1), .out2(decoder_3_out2), .out3(decoder_3_out3),
    .out4(decoder_3_out4), .out5(decoder_3_out5), .out6(decoder_3_out6), .out7(decoder_3_out7), .sel(rt));
  // Probe on r7
  assign rsval = decoder_2_out5 ? r5 : 16'bz;  // Controlled_Buffer controlled_buffer_5
  assign rsval = decoder_2_out4 ? r4 : 16'bz;  // Controlled_Buffer controlled_buffer_6
  assign rsval = decoder_2_out3 ? r3 : 16'bz;  // Controlled_Buffer controlled_buffer_7
  assign rsval = decoder_2_out2 ? r2 : 16'bz;  // Controlled_Buffer controlled_buffer_8
  assign rtval = decoder_3_out5 ? r5 : 16'bz;  // Controlled_Buffer controlled_buffer_9
  assign rtval = decoder_3_out4 ? r4 : 16'bz;  // Controlled_Buffer controlled_buffer_10
  assign rtval = decoder_3_out3 ? r3 : 16'bz;  // Controlled_Buffer controlled_buffer_11
  assign rtval = decoder_3_out2 ? r2 : 16'bz;  // Controlled_Buffer controlled_buffer_12
  assign rsval = decoder_2_out7 ? r7 : 16'bz;  // Controlled_Buffer controlled_buffer_13
  assign rsval = decoder_2_out6 ? r6 : 16'bz;  // Controlled_Buffer controlled_buffer_14
  assign rtval = decoder_3_out7 ? r7 : 16'bz;  // Controlled_Buffer controlled_buffer_15
  assign rtval = decoder_3_out6 ? r6 : 16'bz;  // Controlled_Buffer controlled_buffer_16

  // Other names for the same wires on the sheet: WriteData[15:0] = rdval
endmodule

module ALU (
  input  [15:0] InputData1,
  input  [15:0] InputData2,
  input  [2:0] Shift_Amount,
  input  [2:0] ALUOpType,
  output [15:0] OutputData,
  output Z,
  output Remain,
  output Overflow
);

  wire Acarry, Aovf, nor_1_out, Scarry, Sovf;
  wire [15:0] Add_result, left_shifter_1_output, Not_out, right_shifter_1_output, Sub_result, XOR_out;

  assign Not_out = ~InputData1;  // NOT_Gate Not, 16 bits wide
  Left_Shifter left_shifter_1 (.Input(InputData1), .Shift(Shift_Amount), .Output(left_shifter_1_output));
  Right_Shifter right_shifter_1 (.Input(InputData1), .Shift(Shift_Amount), .Output(right_shifter_1_output));
  assign XOR_out = InputData1 ^ InputData2;  // XOR_Gate XOR, 16 bits wide
  _16_bit_adder Add (.C_out(Acarry), .sub(1'b0), .ovf(Aovf), .B(InputData2), .A(InputData1), .Result(Add_result));
  _16_bit_adder Sub (.C_out(Scarry), .sub(1'b1), .ovf(Sovf), .B(InputData2), .A(InputData1), .Result(Sub_result));
  nor nor_1 (nor_1_out, ALUOpType[2], ALUOpType[1]);
  Multiplexer #(.disabled(0)) multiplexer_1 (
    .in0(Aovf), .in1(Sovf), .out(Overflow), .sel(ALUOpType[0]), .en(nor_1_out));
  Multiplexer #(.select(3), .width(16), .enable("false")) multiplexer_2 (
    .in0(Add_result), .in1(Sub_result), .in2(Not_out), .in3(XOR_out), .in4(left_shifter_1_output),
    .in5(right_shifter_1_output), .out(OutputData), .sel(ALUOpType));  // open: in6, in7
  or or_1 (Z, OutputData[0], OutputData[1], OutputData[2], OutputData[3], OutputData[4], OutputData[5], OutputData[6], OutputData[7], OutputData[9], OutputData[10], OutputData[11], OutputData[12], OutputData[13], OutputData[14], OutputData[15], OutputData[8]);

  assign Remain = OutputData[15];

  // Other names for the same wires on the sheet: ALUop[2:0] = ALUOpType; shft[2:0] = Shift_Amount
endmodule

// SRL
module Right_Shifter (
  input  [15:0] Input,
  input  [2:0] Shift,
  output [15:0] Output
);

  wire multiplexer_1_out, multiplexer_2_out, multiplexer_3_out, multiplexer_4_out, multiplexer_5_out,
       multiplexer_6_out, multiplexer_7_out, multiplexer_8_out, multiplexer_9_out, multiplexer_10_out,
       multiplexer_11_out, multiplexer_12_out, multiplexer_13_out, multiplexer_14_out, multiplexer_15_out,
       multiplexer_16_out, multiplexer_17_out, multiplexer_19_out, multiplexer_20_out, multiplexer_21_out,
       multiplexer_22_out, multiplexer_23_out, multiplexer_24_out, multiplexer_28_out, multiplexer_29_out,
       multiplexer_30_out, multiplexer_31_out, multiplexer_32_out, multiplexer_35_out, multiplexer_36_out,
       multiplexer_40_out, multiplexer_41_out;

  Multiplexer #(.enable("false")) multiplexer_1 (
    .in0(Input[0]), .in1(Input[1]), .out(multiplexer_1_out), .sel(Shift[0]));
  Multiplexer #(.enable("false")) multiplexer_2 (
    .in0(Input[1]), .in1(Input[2]), .out(multiplexer_2_out), .sel(Shift[0]));
  Multiplexer #(.enable("false")) multiplexer_3 (
    .in0(Input[2]), .in1(Input[3]), .out(multiplexer_3_out), .sel(Shift[0]));
  Multiplexer #(.enable("false")) multiplexer_4 (
    .in0(multiplexer_1_out), .in1(multiplexer_3_out), .out(multiplexer_4_out), .sel(Shift[1]));
  Multiplexer #(.enable("false")) multiplexer_5 (
    .in0(Input[3]), .in1(Input[4]), .out(multiplexer_5_out), .sel(Shift[0]));
  Multiplexer #(.enable("false")) multiplexer_6 (
    .in0(Input[4]), .in1(Input[5]), .out(multiplexer_6_out), .sel(Shift[0]));
  Multiplexer #(.enable("false")) multiplexer_7 (
    .in0(Input[5]), .in1(Input[6]), .out(multiplexer_7_out), .sel(Shift[0]));
  Multiplexer #(.enable("false")) multiplexer_8 (
    .in0(multiplexer_2_out), .in1(multiplexer_5_out), .out(multiplexer_8_out), .sel(Shift[1]));
  Multiplexer #(.enable("false")) multiplexer_9 (
    .in0(multiplexer_3_out), .in1(multiplexer_6_out), .out(multiplexer_9_out), .sel(Shift[1]));
  Multiplexer #(.enable("false")) multiplexer_10 (
    .in0(multiplexer_5_out), .in1(multiplexer_7_out), .out(multiplexer_10_out), .sel(Shift[1]));
  Multiplexer #(.enable("false")) multiplexer_11 (
    .in0(Input[6]), .in1(Input[7]), .out(multiplexer_11_out), .sel(Shift[0]));
  Multiplexer #(.enable("false")) multiplexer_12 (
    .in0(Input[7]), .in1(Input[8]), .out(multiplexer_12_out), .sel(Shift[0]));
  Multiplexer #(.enable("false")) multiplexer_13 (
    .in0(Input[8]), .in1(Input[9]), .out(multiplexer_13_out), .sel(Shift[0]));
  Multiplexer #(.enable("false")) multiplexer_14 (
    .in0(multiplexer_6_out), .in1(multiplexer_11_out), .out(multiplexer_14_out), .sel(Shift[1]));
  Multiplexer #(.enable("false")) multiplexer_15 (
    .in0(multiplexer_7_out), .in1(multiplexer_12_out), .out(multiplexer_15_out), .sel(Shift[1]));
  Multiplexer #(.enable("false")) multiplexer_16 (
    .in0(Input[9]), .in1(Input[10]), .out(multiplexer_16_out), .sel(Shift[0]));
  Multiplexer #(.enable("false")) multiplexer_17 (
    .in0(Input[10]), .in1(Input[11]), .out(multiplexer_17_out), .sel(Shift[0]));
  Multiplexer #(.enable("false")) multiplexer_18 (
    .in0(multiplexer_4_out), .in1(multiplexer_14_out), .out(Output[0]), .sel(Shift[2]));
  Multiplexer #(.enable("false")) multiplexer_19 (
    .in0(multiplexer_11_out), .in1(multiplexer_13_out), .out(multiplexer_19_out), .sel(Shift[1]));
  Multiplexer #(.enable("false")) multiplexer_20 (
    .in0(multiplexer_12_out), .in1(multiplexer_16_out), .out(multiplexer_20_out), .sel(Shift[1]));
  Multiplexer #(.enable("false")) multiplexer_21 (
    .in0(multiplexer_13_out), .in1(multiplexer_17_out), .out(multiplexer_21_out), .sel(Shift[1]));
  Multiplexer #(.enable("false")) multiplexer_22 (
    .in0(Input[11]), .in1(Input[12]), .out(multiplexer_22_out), .sel(Shift[0]));
  Multiplexer #(.enable("false")) multiplexer_23 (
    .in0(Input[12]), .in1(Input[13]), .out(multiplexer_23_out), .sel(Shift[0]));
  Multiplexer #(.enable("false")) multiplexer_24 (
    .in0(Input[13]), .in1(Input[14]), .out(multiplexer_24_out), .sel(Shift[0]));
  Multiplexer #(.enable("false")) multiplexer_25 (
    .in0(multiplexer_8_out), .in1(multiplexer_15_out), .out(Output[1]), .sel(Shift[2]));
  Multiplexer #(.enable("false")) multiplexer_26 (
    .in0(multiplexer_9_out), .in1(multiplexer_19_out), .out(Output[2]), .sel(Shift[2]));
  Multiplexer #(.enable("false")) multiplexer_27 (
    .in0(multiplexer_10_out), .in1(multiplexer_20_out), .out(Output[3]), .sel(Shift[2]));
  Multiplexer #(.enable("false")) multiplexer_28 (
    .in0(multiplexer_16_out), .in1(multiplexer_22_out), .out(multiplexer_28_out), .sel(Shift[1]));
  Multiplexer #(.enable("false")) multiplexer_29 (
    .in0(multiplexer_17_out), .in1(multiplexer_23_out), .out(multiplexer_29_out), .sel(Shift[1]));
  Multiplexer #(.enable("false")) multiplexer_30 (
    .in0(multiplexer_22_out), .in1(multiplexer_24_out), .out(multiplexer_30_out), .sel(Shift[1]));
  Multiplexer #(.enable("false")) multiplexer_31 (
    .in0(Input[14]), .in1(Input[15]), .out(multiplexer_31_out), .sel(Shift[0]));
  Multiplexer #(.enable("false")) multiplexer_32 (
    .in0(Input[15]), .in1(1'b0), .out(multiplexer_32_out), .sel(Shift[0]));
  Multiplexer #(.enable("false")) multiplexer_33 (
    .in0(multiplexer_14_out), .in1(multiplexer_21_out), .out(Output[4]), .sel(Shift[2]));
  Multiplexer #(.enable("false")) multiplexer_34 (
    .in0(multiplexer_15_out), .in1(multiplexer_28_out), .out(Output[5]), .sel(Shift[2]));
  Multiplexer #(.enable("false")) multiplexer_35 (
    .in0(multiplexer_23_out), .in1(multiplexer_31_out), .out(multiplexer_35_out), .sel(Shift[1]));
  Multiplexer #(.enable("false")) multiplexer_36 (
    .in0(multiplexer_24_out), .in1(multiplexer_32_out), .out(multiplexer_36_out), .sel(Shift[1]));
  Multiplexer #(.enable("false")) multiplexer_37 (
    .in0(multiplexer_19_out), .in1(multiplexer_29_out), .out(Output[6]), .sel(Shift[2]));
  Multiplexer #(.enable("false")) multiplexer_38 (
    .in0(multiplexer_20_out), .in1(multiplexer_30_out), .out(Output[7]), .sel(Shift[2]));
  Multiplexer #(.enable("false")) multiplexer_39 (
    .in0(multiplexer_21_out), .in1(multiplexer_35_out), .out(Output[8]), .sel(Shift[2]));
  Multiplexer #(.enable("false")) multiplexer_40 (
    .in0(multiplexer_31_out), .in1(1'b0), .out(multiplexer_40_out), .sel(Shift[1]));
  Multiplexer #(.enable("false")) multiplexer_41 (
    .in0(multiplexer_32_out), .in1(1'b0), .out(multiplexer_41_out), .sel(Shift[1]));
  Multiplexer #(.enable("false")) multiplexer_42 (
    .in0(multiplexer_28_out), .in1(multiplexer_36_out), .out(Output[9]), .sel(Shift[2]));
  Multiplexer #(.enable("false")) multiplexer_43 (
    .in0(multiplexer_29_out), .in1(multiplexer_40_out), .out(Output[10]), .sel(Shift[2]));
  Multiplexer #(.enable("false")) multiplexer_44 (
    .in0(multiplexer_30_out), .in1(multiplexer_41_out), .out(Output[11]), .sel(Shift[2]));
  Multiplexer #(.enable("false")) multiplexer_45 (
    .in0(multiplexer_35_out), .in1(1'b0), .out(Output[12]), .sel(Shift[2]));
  Multiplexer #(.enable("false")) multiplexer_46 (
    .in0(multiplexer_36_out), .in1(1'b0), .out(Output[13]), .sel(Shift[2]));
  Multiplexer #(.enable("false")) multiplexer_47 (
    .in0(multiplexer_40_out), .in1(1'b0), .out(Output[14]), .sel(Shift[2]));
  Multiplexer #(.enable("false")) multiplexer_48 (
    .in0(multiplexer_41_out), .in1(1'b0), .out(Output[15]), .sel(Shift[2]));

  // Other names for the same wires on the sheet: S3 = Shift[0]; S2 = Shift[1]; S1 = Shift[2]
endmodule

// SLL
module Left_Shifter (
  input  [15:0] Input,
  input  [2:0] Shift,
  output [15:0] Output
);

  wire multiplexer_1_out, multiplexer_2_out, multiplexer_3_out, multiplexer_4_out, multiplexer_5_out,
       multiplexer_6_out, multiplexer_7_out, multiplexer_8_out, multiplexer_9_out, multiplexer_10_out,
       multiplexer_11_out, multiplexer_12_out, multiplexer_13_out, multiplexer_14_out, multiplexer_15_out,
       multiplexer_16_out, multiplexer_17_out, multiplexer_19_out, multiplexer_20_out, multiplexer_21_out,
       multiplexer_22_out, multiplexer_23_out, multiplexer_24_out, multiplexer_28_out, multiplexer_29_out,
       multiplexer_30_out, multiplexer_31_out, multiplexer_32_out, multiplexer_35_out, multiplexer_36_out,
       multiplexer_40_out, multiplexer_41_out;

  Multiplexer #(.enable("false")) multiplexer_1 (
    .in0(Input[15]), .in1(Input[14]), .out(multiplexer_1_out), .sel(Shift[0]));
  Multiplexer #(.enable("false")) multiplexer_2 (
    .in0(Input[14]), .in1(Input[13]), .out(multiplexer_2_out), .sel(Shift[0]));
  Multiplexer #(.enable("false")) multiplexer_3 (
    .in0(Input[13]), .in1(Input[12]), .out(multiplexer_3_out), .sel(Shift[0]));
  Multiplexer #(.enable("false")) multiplexer_4 (
    .in0(multiplexer_1_out), .in1(multiplexer_3_out), .out(multiplexer_4_out), .sel(Shift[1]));
  Multiplexer #(.enable("false")) multiplexer_5 (
    .in0(Input[12]), .in1(Input[11]), .out(multiplexer_5_out), .sel(Shift[0]));
  Multiplexer #(.enable("false")) multiplexer_6 (
    .in0(Input[11]), .in1(Input[10]), .out(multiplexer_6_out), .sel(Shift[0]));
  Multiplexer #(.enable("false")) multiplexer_7 (
    .in0(Input[10]), .in1(Input[9]), .out(multiplexer_7_out), .sel(Shift[0]));
  Multiplexer #(.enable("false")) multiplexer_8 (
    .in0(multiplexer_2_out), .in1(multiplexer_5_out), .out(multiplexer_8_out), .sel(Shift[1]));
  Multiplexer #(.enable("false")) multiplexer_9 (
    .in0(multiplexer_3_out), .in1(multiplexer_6_out), .out(multiplexer_9_out), .sel(Shift[1]));
  Multiplexer #(.enable("false")) multiplexer_10 (
    .in0(multiplexer_5_out), .in1(multiplexer_7_out), .out(multiplexer_10_out), .sel(Shift[1]));
  Multiplexer #(.enable("false")) multiplexer_11 (
    .in0(Input[9]), .in1(Input[8]), .out(multiplexer_11_out), .sel(Shift[0]));
  Multiplexer #(.enable("false")) multiplexer_12 (
    .in0(Input[8]), .in1(Input[7]), .out(multiplexer_12_out), .sel(Shift[0]));
  Multiplexer #(.enable("false")) multiplexer_13 (
    .in0(Input[7]), .in1(Input[6]), .out(multiplexer_13_out), .sel(Shift[0]));
  Multiplexer #(.enable("false")) multiplexer_14 (
    .in0(multiplexer_6_out), .in1(multiplexer_11_out), .out(multiplexer_14_out), .sel(Shift[1]));
  Multiplexer #(.enable("false")) multiplexer_15 (
    .in0(multiplexer_7_out), .in1(multiplexer_12_out), .out(multiplexer_15_out), .sel(Shift[1]));
  Multiplexer #(.enable("false")) multiplexer_16 (
    .in0(Input[6]), .in1(Input[5]), .out(multiplexer_16_out), .sel(Shift[0]));
  Multiplexer #(.enable("false")) multiplexer_17 (
    .in0(Input[5]), .in1(Input[4]), .out(multiplexer_17_out), .sel(Shift[0]));
  Multiplexer #(.enable("false")) multiplexer_18 (
    .in0(multiplexer_4_out), .in1(multiplexer_14_out), .out(Output[15]), .sel(Shift[2]));
  Multiplexer #(.enable("false")) multiplexer_19 (
    .in0(multiplexer_11_out), .in1(multiplexer_13_out), .out(multiplexer_19_out), .sel(Shift[1]));
  Multiplexer #(.enable("false")) multiplexer_20 (
    .in0(multiplexer_12_out), .in1(multiplexer_16_out), .out(multiplexer_20_out), .sel(Shift[1]));
  Multiplexer #(.enable("false")) multiplexer_21 (
    .in0(multiplexer_13_out), .in1(multiplexer_17_out), .out(multiplexer_21_out), .sel(Shift[1]));
  Multiplexer #(.enable("false")) multiplexer_22 (
    .in0(Input[4]), .in1(Input[3]), .out(multiplexer_22_out), .sel(Shift[0]));
  Multiplexer #(.enable("false")) multiplexer_23 (
    .in0(Input[3]), .in1(Input[2]), .out(multiplexer_23_out), .sel(Shift[0]));
  Multiplexer #(.enable("false")) multiplexer_24 (
    .in0(Input[2]), .in1(Input[1]), .out(multiplexer_24_out), .sel(Shift[0]));
  Multiplexer #(.enable("false")) multiplexer_25 (
    .in0(multiplexer_8_out), .in1(multiplexer_15_out), .out(Output[14]), .sel(Shift[2]));
  Multiplexer #(.enable("false")) multiplexer_26 (
    .in0(multiplexer_9_out), .in1(multiplexer_19_out), .out(Output[13]), .sel(Shift[2]));
  Multiplexer #(.enable("false")) multiplexer_27 (
    .in0(multiplexer_10_out), .in1(multiplexer_20_out), .out(Output[12]), .sel(Shift[2]));
  Multiplexer #(.enable("false")) multiplexer_28 (
    .in0(multiplexer_16_out), .in1(multiplexer_22_out), .out(multiplexer_28_out), .sel(Shift[1]));
  Multiplexer #(.enable("false")) multiplexer_29 (
    .in0(multiplexer_17_out), .in1(multiplexer_23_out), .out(multiplexer_29_out), .sel(Shift[1]));
  Multiplexer #(.enable("false")) multiplexer_30 (
    .in0(multiplexer_22_out), .in1(multiplexer_24_out), .out(multiplexer_30_out), .sel(Shift[1]));
  Multiplexer #(.enable("false")) multiplexer_31 (
    .in0(Input[1]), .in1(Input[0]), .out(multiplexer_31_out), .sel(Shift[0]));
  Multiplexer #(.enable("false")) multiplexer_32 (.in0(Input[0]), .in1(1'b0), .out(multiplexer_32_out), .sel(Shift[0]));
  Multiplexer #(.enable("false")) multiplexer_33 (
    .in0(multiplexer_14_out), .in1(multiplexer_21_out), .out(Output[11]), .sel(Shift[2]));
  Multiplexer #(.enable("false")) multiplexer_34 (
    .in0(multiplexer_15_out), .in1(multiplexer_28_out), .out(Output[10]), .sel(Shift[2]));
  Multiplexer #(.enable("false")) multiplexer_35 (
    .in0(multiplexer_23_out), .in1(multiplexer_31_out), .out(multiplexer_35_out), .sel(Shift[1]));
  Multiplexer #(.enable("false")) multiplexer_36 (
    .in0(multiplexer_24_out), .in1(multiplexer_32_out), .out(multiplexer_36_out), .sel(Shift[1]));
  Multiplexer #(.enable("false")) multiplexer_37 (
    .in0(multiplexer_19_out), .in1(multiplexer_29_out), .out(Output[9]), .sel(Shift[2]));
  Multiplexer #(.enable("false")) multiplexer_38 (
    .in0(multiplexer_20_out), .in1(multiplexer_30_out), .out(Output[8]), .sel(Shift[2]));
  Multiplexer #(.enable("false")) multiplexer_39 (
    .in0(multiplexer_21_out), .in1(multiplexer_35_out), .out(Output[7]), .sel(Shift[2]));
  Multiplexer #(.enable("false")) multiplexer_40 (
    .in0(multiplexer_31_out), .in1(1'b0), .out(multiplexer_40_out), .sel(Shift[1]));
  Multiplexer #(.enable("false")) multiplexer_41 (
    .in0(multiplexer_32_out), .in1(1'b0), .out(multiplexer_41_out), .sel(Shift[1]));
  Multiplexer #(.enable("false")) multiplexer_42 (
    .in0(multiplexer_28_out), .in1(multiplexer_36_out), .out(Output[6]), .sel(Shift[2]));
  Multiplexer #(.enable("false")) multiplexer_43 (
    .in0(multiplexer_29_out), .in1(multiplexer_40_out), .out(Output[5]), .sel(Shift[2]));
  Multiplexer #(.enable("false")) multiplexer_44 (
    .in0(multiplexer_30_out), .in1(multiplexer_41_out), .out(Output[4]), .sel(Shift[2]));
  Multiplexer #(.enable("false")) multiplexer_45 (
    .in0(multiplexer_35_out), .in1(1'b0), .out(Output[3]), .sel(Shift[2]));
  Multiplexer #(.enable("false")) multiplexer_46 (
    .in0(multiplexer_36_out), .in1(1'b0), .out(Output[2]), .sel(Shift[2]));
  Multiplexer #(.enable("false")) multiplexer_47 (
    .in0(multiplexer_40_out), .in1(1'b0), .out(Output[1]), .sel(Shift[2]));
  Multiplexer #(.enable("false")) multiplexer_48 (
    .in0(multiplexer_41_out), .in1(1'b0), .out(Output[0]), .sel(Shift[2]));

  // Other names for the same wires on the sheet: S3 = Shift[0]; S2 = Shift[1]; S1 = Shift[2]
endmodule

module full_adder (
  input  C_in,
  input  in_2,
  input  in_3,
  output Sum,
  output C_out
);

  wire and_1_out, and_2_out, xor_1_out;

  and and_1 (and_1_out, in_3, in_2);
  xor xor_1 (xor_1_out, in_2, in_3);
  or or_1 (C_out, and_1_out, and_2_out);
  and and_2 (and_2_out, xor_1_out, C_in);
  xor xor_2 (Sum, C_in, xor_1_out);
endmodule

// adder
module _16_bit_adder (
  input  sub,
  input  [15:0] A,
  input  [15:0] B,
  output C_out,
  output [15:0] Result,
  output ovf
);

  wire full_adder_1_c_out, full_adder_2_c_out, full_adder_3_c_out, full_adder_4_c_out, full_adder_5_c_out,
       full_adder_6_c_out, full_adder_7_c_out, full_adder_8_c_out, full_adder_9_c_out, full_adder_10_c_out,
       full_adder_11_c_out, full_adder_12_c_out, full_adder_13_c_out, full_adder_14_c_out,
       full_adder_15_c_out, full_adder_16_c_out, xor_2_out, xor_4_out, xor_5_out, xor_6_out, xor_7_out,
       xor_8_out, xor_9_out, xor_10_out, xor_11_out, xor_12_out, xor_13_out, xor_14_out, xor_15_out,
       xor_16_out, xor_17_out, xor_18_out, xor_19_out;

  xor xor_1 (C_out, sub, full_adder_1_c_out);
  xor xor_2 (xor_2_out, B[15], sub);
  full_adder full_adder_1 (
    .in_2(xor_2_out), .in_3(A[15]), .C_in(full_adder_2_c_out), .C_out(full_adder_1_c_out), .Sum(Result[15]));
  xor xor_3 (ovf, full_adder_1_c_out, full_adder_2_c_out);
  xor xor_4 (xor_4_out, B[14], sub);
  full_adder full_adder_2 (
    .in_2(xor_4_out), .in_3(A[14]), .C_in(full_adder_3_c_out), .C_out(full_adder_2_c_out), .Sum(Result[14]));
  xor xor_5 (xor_5_out, B[13], sub);
  full_adder full_adder_3 (
    .in_2(xor_5_out), .in_3(A[13]), .C_in(full_adder_4_c_out), .C_out(full_adder_3_c_out), .Sum(Result[13]));
  xor xor_6 (xor_6_out, B[12], sub);
  full_adder full_adder_4 (
    .in_2(xor_6_out), .in_3(A[12]), .C_in(full_adder_5_c_out), .C_out(full_adder_4_c_out), .Sum(Result[12]));
  xor xor_7 (xor_7_out, B[11], sub);
  full_adder full_adder_5 (
    .in_2(xor_7_out), .in_3(A[11]), .C_in(full_adder_6_c_out), .C_out(full_adder_5_c_out), .Sum(Result[11]));
  xor xor_8 (xor_8_out, B[10], sub);
  full_adder full_adder_6 (
    .in_2(xor_8_out), .in_3(A[10]), .C_in(full_adder_7_c_out), .C_out(full_adder_6_c_out), .Sum(Result[10]));
  xor xor_9 (xor_9_out, B[9], sub);
  full_adder full_adder_7 (
    .in_2(xor_9_out), .in_3(A[9]), .C_in(full_adder_8_c_out), .C_out(full_adder_7_c_out), .Sum(Result[9]));
  xor xor_10 (xor_10_out, B[8], sub);
  full_adder full_adder_8 (
    .in_2(xor_10_out), .in_3(A[8]), .C_in(full_adder_9_c_out), .C_out(full_adder_8_c_out), .Sum(Result[8]));
  xor xor_11 (xor_11_out, B[7], sub);
  full_adder full_adder_9 (
    .in_2(xor_11_out), .in_3(A[7]), .C_in(full_adder_10_c_out), .C_out(full_adder_9_c_out), .Sum(Result[7]));
  xor xor_12 (xor_12_out, B[6], sub);
  full_adder full_adder_10 (
    .in_2(xor_12_out), .in_3(A[6]), .C_in(full_adder_11_c_out), .C_out(full_adder_10_c_out), .Sum(Result[6]));
  full_adder full_adder_11 (
    .in_2(xor_13_out), .in_3(A[5]), .C_in(full_adder_12_c_out), .C_out(full_adder_11_c_out), .Sum(Result[5]));
  xor xor_13 (xor_13_out, B[5], sub);
  xor xor_14 (xor_14_out, B[4], sub);
  full_adder full_adder_12 (
    .in_2(xor_14_out), .in_3(A[4]), .C_in(full_adder_13_c_out), .C_out(full_adder_12_c_out), .Sum(Result[4]));
  xor xor_15 (xor_15_out, B[3], sub);
  full_adder full_adder_13 (
    .in_2(xor_15_out), .in_3(A[3]), .C_in(full_adder_14_c_out), .C_out(full_adder_13_c_out), .Sum(Result[3]));
  xor xor_16 (xor_16_out, B[2], sub);
  full_adder full_adder_14 (
    .in_2(xor_16_out), .in_3(A[2]), .C_in(full_adder_15_c_out), .C_out(full_adder_14_c_out), .Sum(Result[2]));
  xor xor_17 (xor_17_out, B[1], sub);
  full_adder full_adder_15 (
    .in_2(xor_17_out), .in_3(A[1]), .C_in(full_adder_16_c_out), .C_out(full_adder_15_c_out), .Sum(Result[1]));
  full_adder full_adder_16 (
    .in_2(xor_18_out), .in_3(A[0]), .C_in(xor_19_out), .C_out(full_adder_16_c_out), .Sum(Result[0]));
  xor xor_18 (xor_18_out, sub, B[0]);
  xor xor_19 (xor_19_out, sub, 1'b0);
endmodule

module Decoder (
  input  [15:0] Input,
  output [2:0] Rs,
  output [2:0] Rt,
  output [2:0] Rd,
  output [2:0] Shamt,
  output [5:0] Immediate,
  output [3:0] Opcode,
  output [11:0] Address
);


  assign Address = Input[11:0];
  assign Immediate = Input[5:0];
  assign Opcode = Input[15:12];
  assign Rd = Input[5:3];
  assign Rs = Input[11:9];
  assign Rt = Input[8:6];
  assign Shamt = Input[2:0];
endmodule

module Control (
  input  [3:0] opcode,
  output add,
  output addi,
  output sub,
  output \not ,
  output \xor ,
  output sll,
  output srl,
  output lw,
  output sw,
  output bne,
  output blt,
  output j,
  output jr,
  output jal,
  output \input ,
  output \output ,
  output Rwe,
  output ALUinB,
  output Rdst,
  output BR,
  output JP,
  output DMwe,
  output Rwd,
  output Bne_2,
  output Jr_2,
  output In,
  output Out,
  output [2:0] ALUOpCode
);

  Decoder_part #(.select(4), .enable("false")) decoder_1 (
    .out0(add), .out1(addi), .out2(sub), .out3(\not ), .out4(\xor ), .out5(sll), .out6(srl), .out7(lw),
    .out8(DMwe), .out9(bne), .out10(blt), .out11(j), .out12(jr), .out13(jal), .out14(In), .out15(Out),
    .sel(opcode));
  or or_1 (ALUOpCode[2], sll, srl);
  or or_2 (ALUOpCode[0], bne, \xor , sub, srl, blt);
  or or_3 (ALUOpCode[1], \xor , \not );
  or u_Rwe (Rwe, add, addi, sub, \not , \xor , sll, srl, lw, jal, In);
  or u_ALUinB (ALUinB, addi, lw, DMwe);
  or u_Rdst (Rdst, addi, lw, In);
  or u_BR (BR, bne, blt);
  or u_JP (JP, j, jal);

  assign Bne_2 = bne;
  assign \input  = In;
  assign Jr_2 = jr;
  assign \output  = Out;
  assign Rwd = lw;
  assign sw = DMwe;

  // Notes on the sheet:
  //   0 = Add
  //   2 = Not
  //   4 = SLL
  //   ALU Opcodes:
  //   1 = Subtract
  //   3 = XOR
  //   5 = SRL
  //   Instructions
  //   Controls Needed
  //   Controls Done
  //   BR
  //   JP
  //   Rdst
  //   ALUinB
  //   DMwe
  //   Rwd
  //   ALUop
  //   Rwe
  //   Notes
  //   Only SW
  //   Only LW
endmodule
